# Fritzing sketch Dweller Schematic (saved by Fritzing 0.9.9b)
breadboards: 2

parts:
  Accelerometer = Triple Axis Accelerometer Breakout - ADXL345
  2_4Ghz_Transmitter = NRF24L01
  J1 = Piezo Speaker
  LED1 = RGB LED (com. cathode, rgb) [package="5 mm [THT]"]
  R1 = Photocell (LDR) [package=THT]
  R2 = Photocell (LDR) [package=THT]
  R3 = Photocell (LDR) [package=THT]
  Potentiometer = YL-83 Rain Sensor - Control Board
  R5 = Resistor [tolerance=±5% resistance=100 package="1206 [SMD]"]
  Arduino_Uno = Arduino Uno (Rev3)
  NFC_Reader = RFID-RC522-v3
  R6 = Resistor [tolerance=±5% resistance=100k package="0402 [SMD]"]
  R7 = Resistor [tolerance=±5% resistance=100k package="0402 [SMD]"]
  R8 = Resistor [tolerance=±5% resistance=100k package="0402 [SMD]"]
  S1 = SWITCH-MOMENTARY-2 [package=tactile-switch-1101ne]

nets (from the schematic view):
  GND: Accelerometer.GND, 2_4Ghz_Transmitter.GND, LED1.common_cathode, Potentiometer.GND, R5.Pin_1, Arduino_Uno.GND, NFC_Reader.GND, R6.Pin_0, R7.Pin_0, R8.Pin_0
  VCC: Accelerometer.VCC, 2_4Ghz_Transmitter.VCC, Arduino_Uno.3V3, NFC_Reader.3.3V
  N1: Accelerometer.SDA, Arduino_Uno.A4/SDA
  N2: Accelerometer.SCL, Arduino_Uno.A5/SCL
  N3: 2_4Ghz_Transmitter.MOSI, Arduino_Uno.D11_PWM/MOSI, NFC_Reader.MOSI
  N4: 2_4Ghz_Transmitter.CSN, Arduino_Uno.D8
  N5: 2_4Ghz_Transmitter.MISO, Arduino_Uno.D12/MISO, NFC_Reader.MISO
  N6: 2_4Ghz_Transmitter.SCK, Arduino_Uno.D13/SCK, NFC_Reader.SCK
  N7: 2_4Ghz_Transmitter.CE, Arduino_Uno.D7
  N8: J1.pin1, R5.Pin_0
  N9: J1.pin2, Arduino_Uno.D4
  N10: LED1.red_anode, Arduino_Uno.D6_PWM
  N11: LED1.green_anode, Arduino_Uno.D5_PWM
  N12: LED1.blue_anode, Arduino_Uno.D3_PWM
  N13: R1.pin_0, Arduino_Uno.A3, R6.Pin_1
  VCC_2: R1.pin_1, R2.pin_1, R3.pin_1, Potentiometer.VCC, Arduino_Uno.5V
  N14: R2.pin_0, Arduino_Uno.A2, R7.Pin_1
  N15: R3.pin_0, Arduino_Uno.A1, R8.Pin_1
  N16: Potentiometer.AO, Arduino_Uno.A0
  N17: Potentiometer.POS, S1.1
  N18: Potentiometer.NEG, S1.2
  N19: Arduino_Uno.D9_PWM, NFC_Reader.RST
  N20: Arduino_Uno.D10_PWM/SS, NFC_Reader.SDA

custom parts:
  YL-83 Rain Sensor - Control Board: The YL-83 is a rain sensor that has more resistance when dry and less resistance when wet. The module runs at 5V.
  RFID-RC522-v3: A simple China made RFID-RC522 Reader (6x4 cm); do check the pin labels, as this is a MFRC522 based clone.
