# Fritzing sketch Overseer Schematic (saved by Fritzing 0.9.9b)
breadboards: 1

parts:
  U1 = ESP32-38PinWide [part_number=ESP32-38PinWide]
  Part1 = NRF24L01+ Breakout Board
  LED1 = LED - 5mm [color="Red (633nm)" current=0.030 package="5 mm [THT]"]
  LED2 = LED - 5mm [color="Green (555nm)" current=0.030 package="5 mm [THT]"]
  LED3 = LED - 5mm [color="Blue (470nm)" current=0.030 package="5 mm [THT]"]
  R1 = Resistor [tolerance=±5% resistance=330 package="0603 [SMD]"]
  R2 = Resistor [tolerance=±5% resistance=330 package="0603 [SMD]"]
  R3 = Resistor [tolerance=±5% resistance=330 package="0603 [SMD]"]

nets:
  N1: U1.3.3, Part1.VCC
  N2: U1.GPIO32, R2.Pin_1
  N3: U1.GPIO33, R1.Pin_1
  GND: U1.GND, Part1.GND, LED1.cathode, LED2.cathode, LED3.cathode
  N4: U1.VIN, R3.Pin_1
  N5: U1.GPIO4, Part1.CE
  N6: U1.GPIO5, Part1.CS
  N7: U1.GPIO18, Part1.SCK
  N8: U1.GPIO19, Part1.MISO
  N9: U1.GPIO23, Part1.MOSI
  N10: LED1.anode, R3.Pin_0
  N11: LED2.anode, R2.Pin_0
  N12: LED3.anode, R1.Pin_0

custom parts:
  ESP32-38PinWide: Generic 38-Pin ESP32 with wide format (only access to one side of pins on a breadboard) based on Stephen Lilley's HiLetgo ESP-WROOM-32 ESP32 ESP-32S Development Board.
